# Fritzing sketch Untitled Sketch 2 (saved by Fritzing 0.9.3b)

parts:
  Part1 = Bluetooth HC-05 Macho
  Part2 = Arduino Nano (Rev3.0) (ICSP)
  J1 = Basic Servo  # not connected
  J2 = Basic Servo
  J3 = Piezo Speaker  # not connected

nets:
  N1: Part1.TXD, Part2.D2
  VCC: Part1.VCC, Part2.5V, J2.vcc
  GND: Part1.GND, Part2.GND
